// Logisim project cpu.circ as structural Verilog: 4 circuits, main circuit main
module main (
);

  wire and_1_out, button_1_out, CLK, cpu_1_mi, cpu_1_mo, cpu_clock_out, tick_out;
  wire [3:0] cpu_1_data_out, cpu_1_data_out_2, cpu_1_data_out_2_2, cpu_1_data_out_2_3;
  wire [7:0] cpu_1_ram_addr, cpu_1_ram_data, RAM_SV, ROM_SV;

  Clock cpu_clock (.out(cpu_clock_out));
  Button tick (.out(tick_out));
  and and_1 (and_1_out, cpu_clock_out, 1'b1);
  or or_1 (CLK, and_1_out, tick_out);
  Button button_1 (.out(button_1_out));
  Hex_Digit_Display hex_digit_display_1 (.value(cpu_1_data_out_2));  // open: dp
  Hex_Digit_Display hex_digit_display_2 (.value(cpu_1_data_out));  // open: dp
  Hex_Digit_Display hex_digit_display_3 (.value(cpu_1_data_out_2_3));  // open: dp
  Hex_Digit_Display hex_digit_display_4 (.value(cpu_1_data_out_2_2));  // open: dp
  CPU cpu_1 (
    .CLK(CLK), .ROM_INPUT(ROM_SV), .RAM_INPUT(RAM_SV), .DATA_IN(8'hee), .RESET(button_1_out),
    .RAM_DATA(cpu_1_ram_data), .MO(cpu_1_mo), .MI(cpu_1_mi), .RAM_ADDR(cpu_1_ram_addr),
    .DATA_OUT({cpu_1_data_out_2, cpu_1_data_out}), .DATA_OUT_2({cpu_1_data_out_2_3, cpu_1_data_out_2_2}));  // open: DATA_IN_2
  RAM PC_RAM (.addr(cpu_1_ram_addr), .we(cpu_1_mi), .oe(cpu_1_mo), .clk(CLK), .din(cpu_1_ram_data), .dout(RAM_SV));
  ROM PC_ROM (.addr(cpu_1_ram_addr), .data(ROM_SV));
  Hex_Digit_Display hex_digit_display_5 (.value(RAM_SV[7:4]));  // open: dp
  Hex_Digit_Display hex_digit_display_6 (.value(RAM_SV[3:0]));  // open: dp

  // Notes on the sheet:
  //   OUT 1
  //   OUT 2
  //   contents of PC_ROM (hex, n*v repeats v):
  //   d 18 1b 1a 8 4 2 e1 19 e b 14 b e 4 12 b e 1d e1 f 1 1a 1 1d e1 229*ff
  //   OUT 1
endmodule

module CPU (
  input  CLK,
  input  [7:0] ROM_INPUT,
  input  [7:0] RAM_INPUT,
  input  [7:0] DATA_IN,
  input  [7:0] DATA_IN_2,
  input  RESET,
  output [7:0] RAM_DATA,
  output MO,
  output MI,
  output [7:0] RAM_ADDR,
  output [7:0] DATA_OUT,
  output [7:0] DATA_OUT_2
);

  wire AC, AFO, AO, CE, CI, CO, II, INSTRUCTION_CONTROLLER_aa, INSTRUCTION_CONTROLLER_ala,
       INSTRUCTION_CONTROLLER_alo, INSTRUCTION_CONTROLLER_as, INV, INV2, LRA, LRB, MRO, MS, not_1_out,
       not_2_out, not_3_out, or_1_out, ORA, ORB, OUTV, OUTV2, SD, SE, SO;
  wire [2:0] ALU_OP;
  wire [7:0] adder_1_out, adder_2_out, alu_1_d_out, alu_1_flags, ARV, BRV, controlled_buffer_1_out,
       controlled_buffer_8_out, I_REG, PC_q, SP_q, subtractor_1_out;

  assign controlled_buffer_1_out = CI ? RAM_DATA : 8'bz;  // Controlled_Buffer controlled_buffer_1
  not not_1 (not_1_out, CI);
  assign controlled_buffer_1_out = not_1_out ? adder_1_out : 8'bz;  // Controlled_Buffer controlled_buffer_2
  Register PC (.D(controlled_buffer_1_out), .en(or_1_out), .clk(CLK), .Q(PC_q), .clr(RESET));
  or or_1 (or_1_out, CI, CE);
  Register IR (.D(RAM_DATA), .en(II), .clk(CLK), .Q(I_REG), .clr(RESET));
  Register SP (.D(controlled_buffer_8_out), .en(SE), .clk(CLK), .Q(SP_q), .clr(RESET));
  assign RAM_DATA = MRO ? ROM_INPUT : 8'bz;  // Controlled_Buffer controlled_buffer_3
  assign RAM_DATA = MO ? RAM_INPUT : 8'bz;  // Controlled_Buffer controlled_buffer_4
  assign RAM_DATA = INV ? DATA_IN : 8'bz;  // Controlled_Buffer controlled_buffer_5
  assign RAM_DATA = CO ? PC_q : 8'bz;  // Controlled_Buffer controlled_buffer_6
  Adder adder_1 (.a(PC_q), .b(8'h1), .out(adder_1_out));  // open: cin, cout
  Adder adder_2 (.a(SP_q), .b(8'h1), .out(adder_2_out));  // open: cin, cout
  Subtractor subtractor_1 (.a(SP_q), .b(8'h1), .out(subtractor_1_out));  // open: bin, bout
  assign RAM_DATA = SO ? SP_q : 8'bz;  // Controlled_Buffer controlled_buffer_7
  not not_2 (not_2_out, SD);
  assign controlled_buffer_8_out = not_2_out ? adder_2_out : 8'bz;  // Controlled_Buffer controlled_buffer_8
  assign controlled_buffer_8_out = SD ? subtractor_1_out : 8'bz;  // Controlled_Buffer controlled_buffer_9
  not not_3 (not_3_out, CLK);
  Register R_ADDR (.D(RAM_DATA), .en(MS), .clk(CLK), .Q(RAM_ADDR), .clr(RESET));
  assign RAM_DATA = INV2 ? DATA_IN_2 : 8'bz;  // Controlled_Buffer controlled_buffer_10
  control INSTRUCTION_CONTROLLER (
    .CLK(not_3_out), .RESET(RESET), .I_REG(I_REG), .MAIN_BUS(RAM_DATA), .OUTV2(OUTV2), .INV2(INV2),
    .OUTV(OUTV), .INV(INV), .ORB(ORB), .ORA(ORA), .LRB(LRB), .LRA(LRA), .AFO(AFO),
    .ALO(INSTRUCTION_CONTROLLER_alo), .ALA(INSTRUCTION_CONTROLLER_ala), .AA(INSTRUCTION_CONTROLLER_aa),
    .AS(INSTRUCTION_CONTROLLER_as), .AC(AC), .AO(AO), .II(II), .MRO(MRO), .MO(MO), .MI(MI), .MS(MS), .SD(SD),
    .SE(SE), .SO(SO), .CE(CE), .CI(CI), .CO(CO));  // open: HLT, SI1, SI
  Priority_Encoder priority_encoder_1 (
    .in0(INSTRUCTION_CONTROLLER_aa), .in1(INSTRUCTION_CONTROLLER_as), .in2(INSTRUCTION_CONTROLLER_ala),
    .in3(INSTRUCTION_CONTROLLER_alo), .out(ALU_OP));  // open: in4, in5, in6, in7, en_in, gs, en_out
  Register AR (.D(RAM_DATA), .en(LRA), .clk(CLK), .Q(ARV), .clr(RESET));
  Register BR (.D(RAM_DATA), .en(LRB), .clk(CLK), .Q(BRV), .clr(RESET));
  assign RAM_DATA = ORA ? ARV : 8'bz;  // Controlled_Buffer controlled_buffer_11
  assign RAM_DATA = ORB ? BRV : 8'bz;  // Controlled_Buffer controlled_buffer_12
  Register OUT1 (.D(RAM_DATA), .en(OUTV), .clk(CLK), .Q(DATA_OUT), .clr(RESET));
  Register OUT2 (.D(RAM_DATA), .en(OUTV2), .clk(CLK), .Q(DATA_OUT_2), .clr(RESET));
  assign RAM_DATA = AO ? alu_1_d_out : 8'bz;  // Controlled_Buffer controlled_buffer_13
  ALU alu_1 (.A_IN(ARV), .B_IN(BRV), .CIN(AC), .OP(ALU_OP), .D_OUT(alu_1_d_out), .FLAGS(alu_1_flags));  // open: COUT
  assign RAM_DATA = AFO ? alu_1_flags : 8'bz;  // Controlled_Buffer controlled_buffer_14

  // Other names for the same wires on the sheet: FORCE_RESET = RESET; MAIN_BUS[7:0] = RAM_DATA
endmodule

module control (
  input  CLK,
  input  RESET,
  input  [7:0] I_REG,
  input  [7:0] MAIN_BUS,
  output OUTV2,
  output INV2,
  output HLT,
  output SI1,
  output SI,
  output OUTV,
  output INV,
  output ORB,
  output ORA,
  output LRB,
  output LRA,
  output AFO,
  output ALO,
  output ALA,
  output AA,
  output AS,
  output AC,
  output AO,
  output II,
  output MRO,
  output MO,
  output MI,
  output MS,
  output SD,
  output SE,
  output SO,
  output CE,
  output CI,
  output CO
);

  wire and_1_out, buffer_2_out, CI_R, not_1_out, not_2_out;
  wire [2:0] adder_1_out, CI_C_q, controlled_buffer_1_out;
  wire [31:0] INSTRUCTIONS_data;
  wire [31:29] buffer_1_out;

  not not_1 (not_1_out, CI_R);
  Register #(.width(3)) CI_C (.D(controlled_buffer_1_out), .en(CLK), .clk(CLK), .Q(CI_C_q), .clr(RESET));
  assign controlled_buffer_1_out = CI_R ? 3'b000 : 3'bz;  // Controlled_Buffer controlled_buffer_1
  assign controlled_buffer_1_out = not_1_out ? adder_1_out : 3'bz;  // Controlled_Buffer controlled_buffer_2
  Adder #(.width(3)) adder_1 (.a(CI_C_q), .b(3'b001), .out(adder_1_out));  // open: cin, cout
  ROM #(.addrWidth(11), .dataWidth(32)) INSTRUCTIONS (.addr({I_REG, CI_C_q}), .data(INSTRUCTIONS_data));
  assign {buffer_1_out, OUTV2, INV2, HLT, SI1, SI, OUTV, INV, ORB, ORA, LRB, LRA, AFO, ALO, ALA, AA, AS, AC, AO, II, MRO, MO, MI, MS, SD, SE, SO, CE, CI, CO} = INSTRUCTIONS_data;  // Buffer buffer_1, 32 bits wide
  buf buffer_2 (buffer_2_out, SI);
  and and_1 (and_1_out, SI1, not_2_out);
  not not_2 (not_2_out, MAIN_BUS[0]);
  or or_1 (CI_R, buffer_2_out, and_1_out);

  // Other names for the same wires on the sheet: MB[7:0] = MAIN_BUS

  // Notes on the sheet:
  //   contents of INSTRUCTIONS (hex, n*v repeats v):
  //   41 604 41 244 40100 1000000 1000000 1000000 41 604 41 244 80100 1000000 1000000 1000000 41 604 41
  //   244 100080 1000000 1000000 1000000 41 604 41 244 200080 1000000 1000000 1000000 41 604 44800
  //   5*1000000 41 604 45800 5*1000000 41 604 42800 5*1000000 41 604 6*1000000 41 604 48800 5*1000000 41
  //   604 50800 5*1000000 41 604 6*1000000 41 604 41 202 4*1000000 41 604 2020000 41 202 1000000 1000000
  //   1000000 41 604 30 48 100080 1000000 1000000 1000000 41 604 48 40110 4*1000000 41 604 41 40204
  //   4*1000000 41 604 440000 5*1000000 41 604 480000 5*1000000 41 604 900000 5*1000000 41 604 a00000
  //   5*1000000 41 604 8040000 5*1000000 41 604 8080000 5*1000000 41 604 10100000 5*1000000 41 604
  //   10200000 5*1000000 41 604 30 48 200080 1000000 1000000 1000000 41 604 48 80110 4*1000000 41 604 41
  //   80204 4*1000000 41 604 40001 5*1000000 41 604 100002 5*1000000 41 604 41 244 102 102 1000000 1000000
  //   41 604 6*1000000 41 604 6*1000000 41 604 6*1000000 41 604 6*1000000 41 604 6*1000000 41 604
  //   6*1000000 41 604 6*1000000 41 604 6*1000000 41 604 6*1000000 41 604 6*1000000 41 604 6*1000000 41
  //   604 6*1000000 41 604 6*1000000 41 604 6*1000000 41 604 6*1000000 41 604 6*1000000 41 604 6*1000000
  //   41 604 6*1000000 41 604 6*1000000 41 604 6*1000000 41 604 6*1000000 41 604 6*1000000 41 604
  //   6*1000000 41 604 6*1000000 41 604 6*1000000 41 604 6*1000000 41 604 6*1000000 41 604 6*1000000 41
  //   604 6*1000000 41 604 6*1000000 41 604 6*1000000 41 604 6*1000000 41 604 6*1000000 41 604 6*1000000
  //   41 604 6*1000000 41 604 6*1000000 41 604 6*1000000 41 604 6*1000000 41 604 6*1000000 41 604
  //   6*1000000 41 604 6*1000000 41 604 6*1000000 41 604 6*1000000 41 604 6*1000000 41 604 6*1000000 41
  //   604 6*1000000 41 604 6*1000000 41 604 6*1000000 41 604 6*1000000 41 604 6*1000000 41 604 6*1000000
  //   41 604 6*1000000 41 604 6*1000000 41 604 6*1000000 41 604 6*1000000 41 604 6*1000000 41 604
  //   6*1000000 41 604 6*1000000 41 604 6*1000000 41 604 6*1000000 41 604 6*1000000 41 604 6*1000000 41
  //   604 6*1000000 41 604 6*1000000 41 604 6*1000000 41 604 6*1000000 41 604 6*1000000 41 604 6*1000000
  //   41 604 6*1000000 41 604 6*1000000 41 604 6*1000000 41 604 6*1000000 41 604 6*1000000 41 604
  //   6*1000000 41 604 6*1000000 41 604 6*1000000 41 604 6*1000000 41 604 6*1000000 41 604 6*1000000 41
  //   604 6*1000000 41 604 6*1000000 41 604 6*1000000 41 604 6*1000000 41 604 6*1000000 41 604 6*1000000
  //   41 604 6*1000000 41 604 6*1000000 41 604 6*1000000 41 604 6*1000000 41 604 6*1000000 41 604
  //   6*1000000 41 604 6*1000000 41 604 6*1000000 41 604 6*1000000 41 604 6*1000000 41 604 6*1000000 41
  //   604 6*1000000 41 604 6*1000000 41 604 6*1000000 41 604 6*1000000 41 604 6*1000000 41 604 6*1000000
  //   41 604 6*1000000 41 604 6*1000000 41 604 6*1000000 41 604 6*1000000 41 604 6*1000000 41 604
  //   6*1000000 41 604 6*1000000 41 604 6*1000000 41 604 6*1000000 41 604 6*1000000 41 604 6*1000000 41
  //   604 6*1000000 41 604 6*1000000 41 604 6*1000000 41 604 6*1000000 41 604 6*1000000 41 604 6*1000000
  //   41 604 6*1000000 41 604 6*1000000 41 604 6*1000000 41 604 6*1000000 41 604 6*1000000 41 604
  //   6*1000000 41 604 6*1000000 41 604 6*1000000 41 604 6*1000000 41 604 6*1000000 41 604 6*1000000 41
  //   604 6*1000000 41 604 6*1000000 41 604 6*1000000 41 604 6*1000000 41 604 6*1000000 41 604 6*1000000
  //   41 604 6*1000000 41 604 6*1000000 41 604 6*1000000 41 604 6*1000000 41 604 6*1000000 41 604
  //   6*1000000 41 604 6*1000000 41 604 6*1000000 41 604 6*1000000 41 604 6*1000000 41 604 6*1000000 41
  //   604 6*1000000 41 604 6*1000000 41 604 6*1000000 41 604 6*1000000 41 604 6*1000000 41 604 6*1000000
  //   41 604 6*1000000 41 604 6*1000000 41 604 6*1000000 41 604 6*1000000 41 604 6*1000000 41 604
  //   6*1000000 41 604 6*1000000 41 604 6*1000000 41 604 6*1000000 41 604 6*1000000 41 604 6*1000000 41
  //   604 6*1000000 41 604 6*1000000 41 604 6*1000000 41 604 6*1000000 41 604 6*1000000 41 604 6*1000000
  //   41 604 6*1000000 41 604 6*1000000 41 604 6*1000000 41 604 6*1000000 41 604 6*1000000 41 604
  //   6*1000000 41 604 6*1000000 41 604 6*1000000 41 604 6*1000000 41 604 6*1000000 41 604 6*1000000 41
  //   604 6*1000000 41 604 6*1000000 41 604 6*1000000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
endmodule

module ALU (
  input  [7:0] A_IN,
  input  [7:0] B_IN,
  input  CIN,
  input  [2:0] OP,
  output [7:0] D_OUT,
  output COUT,
  output [7:0] FLAGS
);

  wire adder_1_cout, decoder_1_out0, decoder_1_out1, decoder_1_out2, decoder_1_out3, subtractor_1_bout;
  wire [7:0] adder_1_out, and_1_out, or_2_out, subtractor_1_out;

  Decoder #(.select(3)) decoder_1 (
    .out0(decoder_1_out0), .out1(decoder_1_out1), .out2(decoder_1_out2), .out3(decoder_1_out3), .sel(OP));  // open: out4, out5, out6, out7, en
  assign D_OUT = decoder_1_out0 ? adder_1_out : 8'bz;  // Controlled_Buffer controlled_buffer_1
  Adder adder_1 (.a(A_IN), .b(B_IN), .out(adder_1_out), .cin(CIN), .cout(adder_1_cout));
  assign D_OUT = decoder_1_out1 ? subtractor_1_out : 8'bz;  // Controlled_Buffer controlled_buffer_2
  Subtractor subtractor_1 (.a(A_IN), .b(B_IN), .out(subtractor_1_out), .bin(CIN), .bout(subtractor_1_bout));
  or or_1 (COUT, adder_1_cout, subtractor_1_bout);
  assign and_1_out = A_IN & B_IN;  // AND_Gate and_1, 8 bits wide
  assign D_OUT = decoder_1_out2 ? and_1_out : 8'bz;  // Controlled_Buffer controlled_buffer_3
  assign or_2_out = A_IN | B_IN;  // OR_Gate or_2, 8 bits wide
  assign D_OUT = decoder_1_out3 ? or_2_out : 8'bz;  // Controlled_Buffer controlled_buffer_4

  assign FLAGS = {{7{1'b1}}, COUT};

  // Other names for the same wires on the sheet: C = CIN; DA[7:0] = A_IN; DB[7:0] = B_IN; DO[7:0] = D_OUT; CO = COUT
endmodule
